// Logisim project ALU.circ as structural Verilog: 8 circuits, main circuit main
module main (
  input  [3:0] Op_Code,
  input  [31:0] A,
  input  [31:0] B,
  output [31:0] Result,
  output Zero,
  output overeflow
);

  wire comparator_1_lt, comparator_2_eq;
  wire [31:0] adder_1_out, and_1_out, bit_extender_1_out, multiplier_1_cout, multiplier_1_out, or_1_out,
       shifter_1_out, shifter_2_out, shifter_3_out, subtractor_1_out, xor_1_out;

  Overflow overflow_1 (.A(A), .B(B), .overflow(overeflow));
  Adder #(.width(32)) adder_1 (.a(A), .b(B), .out(adder_1_out));  // open: cin, cout
  Shifter #(.width(32)) shifter_1 (.in(A), .\dist (B[4:0]), .out(shifter_1_out));
  assign xor_1_out = A ^ B;  // XOR_Gate xor_1, 32 bits wide
  Shifter #(.width(32), .shift("lr")) shifter_2 (.in(A), .\dist (B[4:0]), .out(shifter_2_out));
  assign or_1_out = A | B;  // OR_Gate or_1, 32 bits wide
  assign and_1_out = A & B;  // AND_Gate and_1, 32 bits wide
  Multiplier #(.width(32)) multiplier_1 (.a(A), .b(B), .out(multiplier_1_out), .cout(multiplier_1_cout));  // open: cin
  Subtractor #(.width(32)) subtractor_1 (.a(A), .b(B), .out(subtractor_1_out));  // open: bin, bout
  Shifter #(.width(32), .shift("ar")) shifter_3 (.in(A), .\dist (B[4:0]), .out(shifter_3_out));
  Comparator #(.width(32)) comparator_1 (.a(A), .b(B), .lt(comparator_1_lt));  // open: gt, eq
  assign bit_extender_1_out = {{31{comparator_1_lt}}, comparator_1_lt};  // Bit_Extender bit_extender_1
  MUX_16 mux_16_1 (
    .A0(adder_1_out), .A1(shifter_1_out), .A2(bit_extender_1_out), .A4(xor_1_out), .A5(shifter_2_out),
    .A6(or_1_out), .A7(and_1_out), .A8(multiplier_1_out), .A9(multiplier_1_cout), .A13(subtractor_1_out),
    .A14(shifter_3_out), .A15(B), .S0(Op_Code[0]), .S1(Op_Code[1]), .S2(Op_Code[2]), .S3(Op_Code[3]),
    .\output (Result));  // open: A3, A10, A11, A12
  Comparator #(.width(32)) comparator_2 (.a(Result), .b({32{1'b0}}), .eq(comparator_2_eq));  // open: gt, lt
  not not_1 (Zero, comparator_2_eq);

  // Notes on the sheet:
  //   0 -add
  //   1- sll
  //   2 - slt signed
  //   4 - xor
  //   6 - or
  //   7 - and
  //   5 - srl - unsigned shift
  //   8 - mul = ans[31:0]
  //   9 - mulh = ans[63:32]
  //   12 - sub
  //   13 - sra
  //   15 - bsel
  //   0 -add
  //   1- sll
  //   2 - slt signed
  //   3 - unused
  //   4 - xor
  //   5 - srl - unsigned shift
  //   6 - or
  //   7 - and
  //   8 - mul
  //   9 - mulh
  //   10  - unused
  //   11 - mulhu
  //   12 - sub
  //   13 - sra
  //   14 -unused
  //   15 - bsel
  //   14 -unused
  //   11 - mulhu
  //   3 - unused
  //   10  - unused
endmodule

module MUX_2 (
  input  S0,
  input  [31:0] A0,
  input  [31:0] A1,
  output [31:0] \output 
);

  wire [31:0] and_1_out, and_2_out, bit_extender_1_out, not_1_out;

  assign bit_extender_1_out = {{31{S0}}, S0};  // Bit_Extender bit_extender_1
  assign not_1_out = ~bit_extender_1_out;  // NOT_Gate not_1, 32 bits wide
  assign and_1_out = A0 & not_1_out;  // AND_Gate and_1, 32 bits wide
  assign and_2_out = bit_extender_1_out & A1;  // AND_Gate and_2, 32 bits wide
  assign \output  = and_1_out | and_2_out;  // OR_Gate or_1, 32 bits wide
endmodule

module MUX_4 (
  input  S0,
  input  S1,
  input  [31:0] A0,
  input  [31:0] A1,
  input  [31:0] A2,
  input  [31:0] A3,
  output [31:0] \output 
);

  wire [31:0] mux_2_1_output, mux_2_2_output;

  MUX_2 mux_2_1 (.A0(A0), .A1(A1), .S0(S0), .\output (mux_2_1_output));
  MUX_2 mux_2_2 (.A0(A2), .A1(A3), .S0(S0), .\output (mux_2_2_output));
  MUX_2 mux_2_3 (.A0(mux_2_1_output), .A1(mux_2_2_output), .S0(S1), .\output (\output ));
endmodule

module MUX_16 (
  input  S0,
  input  S1,
  input  S2,
  input  S3,
  input  [31:0] A0,
  input  [31:0] A1,
  input  [31:0] A2,
  input  [31:0] A3,
  input  [31:0] A4,
  input  [31:0] A5,
  input  [31:0] A6,
  input  [31:0] A7,
  input  [31:0] A8,
  input  [31:0] A9,
  input  [31:0] A10,
  input  [31:0] A11,
  input  [31:0] A12,
  input  [31:0] A13,
  input  [31:0] A14,
  input  [31:0] A15,
  output [31:0] \output 
);

  wire [31:0] mux_4_1_output, mux_4_2_output, mux_4_3_output, mux_4_4_output;

  MUX_4 mux_4_1 (.A0(A0), .A1(A1), .A2(A2), .A3(A3), .S0(S0), .S1(S1), .\output (mux_4_1_output));
  MUX_4 mux_4_2 (.A0(A4), .A1(A5), .A2(A6), .A3(A7), .S0(S0), .S1(S1), .\output (mux_4_2_output));
  MUX_4 mux_4_3 (.A0(A8), .A1(A9), .A2(A10), .A3(A11), .S0(S0), .S1(S1), .\output (mux_4_3_output));
  MUX_4 mux_4_4 (.A0(A12), .A1(A13), .A2(A14), .A3(A15), .S0(S0), .S1(S1), .\output (mux_4_4_output));
  MUX_4 mux_4_5 (
    .A0(mux_4_1_output), .A1(mux_4_2_output), .A2(mux_4_3_output), .A3(mux_4_4_output), .S0(S2), .S1(S3),
    .\output (\output ));
endmodule

module Overflow (
  input  [31:0] A,
  input  [31:0] B,
  output overflow
);

  wire and_1_out, and_2_out, comparator_1_lt, comparator_2_lt, comparator_3_gt, comparator_4_gt, not_1_out,
       not_2_out, or_1_out, or_2_out, or_3_out, xor_1_out;
  wire [31:0] adder_1_out;

  xor xor_1 (xor_1_out, A[31], B[31]);
  Adder #(.width(32)) adder_1 (.a(A), .b(B), .out(adder_1_out));  // open: cin, cout
  not not_1 (not_1_out, xor_1_out);
  Comparator #(.width(32)) comparator_1 (.a(A), .b(adder_1_out), .lt(comparator_1_lt));  // open: gt, eq
  Comparator #(.width(32)) comparator_2 (.a(B), .b(adder_1_out), .lt(comparator_2_lt));  // open: gt, eq
  Comparator #(.width(32)) comparator_3 (.a(A), .b(adder_1_out), .gt(comparator_3_gt));  // open: eq, lt
  Comparator #(.width(32)) comparator_4 (.a(B), .b(adder_1_out), .gt(comparator_4_gt));  // open: eq, lt
  or or_1 (or_1_out, comparator_3_gt, comparator_4_gt);
  or or_2 (or_2_out, comparator_1_lt, comparator_2_lt);
  not not_2 (not_2_out, A[31]);
  and and_1 (and_1_out, not_2_out, or_1_out);
  and and_2 (and_2_out, A[31], or_2_out);
  or or_3 (or_3_out, and_2_out, and_1_out);
  Small_MUX_2 small_mux_2_1 (.A0(1'b0), .A1(or_3_out), .S0(not_1_out), .\output (overflow));
endmodule

module Small_MUX_2 (
  input  S0,
  input  A0,
  input  A1,
  output \output 
);

  wire and_1_out, and_2_out, not_1_out;

  not not_1 (not_1_out, S0);
  and and_1 (and_1_out, A0, not_1_out);
  and and_2 (and_2_out, S0, A1);
  or or_1 (\output , and_1_out, and_2_out);
endmodule

module MULhu (
  input  [31:0] A,
  input  [31:0] B,
  output [31:0] out_3
);

  wire [31:0] adder_1_out, adder_2_out, bit_extender_1_out, bit_extender_2_out, bit_extender_3_out,
       bit_extender_4_out, multiplier_1_out, multiplier_2_out, multiplier_3_out, multiplier_4_cout,
       shifter_1_out, shifter_2_out, shifter_3_out;

  assign bit_extender_1_out = {{31{1'b0}}, A[31]};  // Bit_Extender bit_extender_1
  assign bit_extender_2_out = {{1{1'b0}}, A[30:0]};  // Bit_Extender bit_extender_2
  assign bit_extender_3_out = {{31{1'b0}}, B[31]};  // Bit_Extender bit_extender_3
  assign bit_extender_4_out = {{1{1'b0}}, B[30:0]};  // Bit_Extender bit_extender_4
  Multiplier #(.width(32)) multiplier_1 (
    .a(bit_extender_1_out), .b(bit_extender_3_out), .out(multiplier_1_out));  // open: cin, cout
  Multiplier #(.width(32)) multiplier_2 (
    .a(bit_extender_2_out), .b(bit_extender_3_out), .out(multiplier_2_out));  // open: cin, cout
  Multiplier #(.width(32)) multiplier_3 (
    .a(bit_extender_1_out), .b(bit_extender_4_out), .out(multiplier_3_out));  // open: cin, cout
  Multiplier #(.width(32)) multiplier_4 (
    .a(bit_extender_2_out), .b(bit_extender_4_out), .cout(multiplier_4_cout));  // open: out, cin
  Shifter #(.width(32)) shifter_1 (.in(multiplier_1_out), .\dist (5'b11110), .out(shifter_1_out));
  Shifter #(.width(32), .shift("lr")) shifter_2 (.in(multiplier_2_out), .\dist (5'b00001), .out(shifter_2_out));
  Shifter #(.width(32), .shift("lr")) shifter_3 (.in(multiplier_3_out), .\dist (5'b00001), .out(shifter_3_out));
  Adder #(.width(32)) adder_1 (.a(shifter_2_out), .b(shifter_3_out), .out(adder_1_out));  // open: cin, cout
  Adder #(.width(32)) adder_2 (.a(adder_1_out), .b(multiplier_4_cout), .out(adder_2_out));  // open: cin, cout
  Adder #(.width(32)) adder_3 (.a(shifter_1_out), .b(adder_2_out), .out(out_3));  // open: cin, cout

  // Notes on the sheet:
  //   a1
  //   a2
  //   b1
  //   b2
  //   a1*b1
  //   a2*b1
  //   a1*b2
  //   a2*b2
endmodule

module ALU (
  input  [3:0] opcode,
  input  [31:0] A,
  input  [31:0] B,
  output [31:0] result,
  output zero,
  output overflow
);

  main main_1 (.A(A), .B(B), .Op_Code(opcode), .Result(result), .Zero(zero), .overeflow(overflow));
endmodule
