// Logisim project register.circ as structural Verilog: 3 circuits, main circuit main
module main (
  input  [4:0] rs1,
  input  [4:0] rs2,
  input  [4:0] rd,
  input  RegWEn,
  input  [31:0] write_data,
  output [31:0] read_data_1,
  output [31:0] read_data_2
);

  wire clk_out;

  Clock clk (.out(clk_out));
  register_file register_file_1 (
    .rs1(rs1), .rs2(rs2), .rd(rd), .RegWEn(RegWEn), .clock(clk_out), .write_data(write_data),
    .read_data_1(read_data_1), .read_data_2(read_data_2));
endmodule

module register_file (
  input  [4:0] rs1,
  input  [4:0] rs2,
  input  [4:0] rd,
  input  RegWEn,
  input  clock,
  input  [31:0] write_data,
  output [31:0] read_data_1,
  output [31:0] read_data_2
);

  wire and_1_out, and_2_out, and_3_out, and_4_out, and_5_out, and_6_out, and_7_out, and_8_out, and_9_out,
       and_10_out, and_11_out, and_12_out, and_13_out, and_14_out, and_15_out, and_16_out, and_17_out,
       and_18_out, and_19_out, and_20_out, and_21_out, and_22_out, and_23_out, and_24_out, and_25_out,
       and_26_out, and_27_out, and_28_out, and_29_out, and_30_out, and_31_out;
  wire [31:0] shifter_1_out, x0_data_out, x1_data_out, x2_data_out, x3_data_out, x4_data_out, x5_data_out,
       x6_data_out, x7_data_out, x8_data_out, x9_data_out, x10_data_out, x11_data_out, x12_data_out,
       x13_data_out, x14_data_out, x15_data_out, x16_data_out, x17_data_out, x18_data_out, x19_data_out,
       x20_data_out, x21_data_out, x22_data_out, x23_data_out, x24_data_out, x25_data_out, x26_data_out,
       x27_data_out, x28_data_out, x29_data_out, x30_data_out, x31_data_out;

  Shifter #(.width(32)) shifter_1 (.in(32'h1), .\dist (rd), .out(shifter_1_out));
  and and_1 (and_1_out, RegWEn, shifter_1_out[1]);
  and and_2 (and_2_out, RegWEn, shifter_1_out[2]);
  and and_3 (and_3_out, RegWEn, shifter_1_out[3]);
  and and_4 (and_4_out, RegWEn, shifter_1_out[4]);
  and and_5 (and_5_out, RegWEn, shifter_1_out[5]);
  and and_6 (and_6_out, RegWEn, shifter_1_out[6]);
  and and_7 (and_7_out, RegWEn, shifter_1_out[7]);
  and and_8 (and_8_out, RegWEn, shifter_1_out[8]);
  and and_9 (and_9_out, RegWEn, shifter_1_out[9]);
  and and_10 (and_10_out, RegWEn, shifter_1_out[10]);
  and and_11 (and_11_out, RegWEn, shifter_1_out[11]);
  and and_12 (and_12_out, RegWEn, shifter_1_out[12]);
  and and_13 (and_13_out, RegWEn, shifter_1_out[13]);
  and and_14 (and_14_out, RegWEn, shifter_1_out[14]);
  and and_15 (and_15_out, RegWEn, shifter_1_out[15]);
  and and_16 (and_16_out, RegWEn, shifter_1_out[16]);
  and and_17 (and_17_out, RegWEn, shifter_1_out[17]);
  and and_18 (and_18_out, RegWEn, shifter_1_out[18]);
  and and_19 (and_19_out, RegWEn, shifter_1_out[19]);
  and and_20 (and_20_out, RegWEn, shifter_1_out[20]);
  and and_21 (and_21_out, RegWEn, shifter_1_out[21]);
  and and_22 (and_22_out, RegWEn, shifter_1_out[22]);
  and and_23 (and_23_out, RegWEn, shifter_1_out[23]);
  and and_24 (and_24_out, RegWEn, shifter_1_out[24]);
  and and_25 (and_25_out, RegWEn, shifter_1_out[25]);
  and and_26 (and_26_out, RegWEn, shifter_1_out[26]);
  and and_27 (and_27_out, RegWEn, shifter_1_out[27]);
  and and_28 (and_28_out, RegWEn, shifter_1_out[28]);
  and and_29 (and_29_out, RegWEn, shifter_1_out[29]);
  and and_30 (and_30_out, RegWEn, shifter_1_out[30]);
  and and_31 (and_31_out, RegWEn, shifter_1_out[31]);
  single_register x0 (.data_in({32{1'b0}}), .write_en(1'b1), .clock(clock), .data_out(x0_data_out));
  single_register x1 (.data_in(write_data), .write_en(and_1_out), .clock(clock), .data_out(x1_data_out));
  single_register x2 (.data_in(write_data), .write_en(and_2_out), .clock(clock), .data_out(x2_data_out));
  single_register x3 (.data_in(write_data), .write_en(and_3_out), .clock(clock), .data_out(x3_data_out));
  single_register x4 (.data_in(write_data), .write_en(and_4_out), .clock(clock), .data_out(x4_data_out));
  single_register x5 (.data_in(write_data), .write_en(and_5_out), .clock(clock), .data_out(x5_data_out));
  single_register x6 (.data_in(write_data), .write_en(and_6_out), .clock(clock), .data_out(x6_data_out));
  single_register x7 (.data_in(write_data), .write_en(and_7_out), .clock(clock), .data_out(x7_data_out));
  single_register x8 (.data_in(write_data), .write_en(and_8_out), .clock(clock), .data_out(x8_data_out));
  single_register x9 (.data_in(write_data), .write_en(and_9_out), .clock(clock), .data_out(x9_data_out));
  single_register x10 (.data_in(write_data), .write_en(and_10_out), .clock(clock), .data_out(x10_data_out));
  single_register x11 (.data_in(write_data), .write_en(and_11_out), .clock(clock), .data_out(x11_data_out));
  single_register x12 (.data_in(write_data), .write_en(and_12_out), .clock(clock), .data_out(x12_data_out));
  single_register x13 (.data_in(write_data), .write_en(and_13_out), .clock(clock), .data_out(x13_data_out));
  single_register x14 (.data_in(write_data), .write_en(and_14_out), .clock(clock), .data_out(x14_data_out));
  single_register x15 (.data_in(write_data), .write_en(and_15_out), .clock(clock), .data_out(x15_data_out));
  single_register x16 (.data_in(write_data), .write_en(and_16_out), .clock(clock), .data_out(x16_data_out));
  single_register x17 (.data_in(write_data), .write_en(and_17_out), .clock(clock), .data_out(x17_data_out));
  single_register x18 (.data_in(write_data), .write_en(and_18_out), .clock(clock), .data_out(x18_data_out));
  single_register x19 (.data_in(write_data), .write_en(and_19_out), .clock(clock), .data_out(x19_data_out));
  single_register x20 (.data_in(write_data), .write_en(and_20_out), .clock(clock), .data_out(x20_data_out));
  single_register x21 (.data_in(write_data), .write_en(and_21_out), .clock(clock), .data_out(x21_data_out));
  single_register x22 (.data_in(write_data), .write_en(and_22_out), .clock(clock), .data_out(x22_data_out));
  single_register x23 (.data_in(write_data), .write_en(and_23_out), .clock(clock), .data_out(x23_data_out));
  single_register x24 (.data_in(write_data), .write_en(and_24_out), .clock(clock), .data_out(x24_data_out));
  single_register x25 (.data_in(write_data), .write_en(and_25_out), .clock(clock), .data_out(x25_data_out));
  single_register x26 (.data_in(write_data), .write_en(and_26_out), .clock(clock), .data_out(x26_data_out));
  single_register x27 (.data_in(write_data), .write_en(and_27_out), .clock(clock), .data_out(x27_data_out));
  single_register x28 (.data_in(write_data), .write_en(and_28_out), .clock(clock), .data_out(x28_data_out));
  single_register x29 (.data_in(write_data), .write_en(and_29_out), .clock(clock), .data_out(x29_data_out));
  single_register x30 (.data_in(write_data), .write_en(and_30_out), .clock(clock), .data_out(x30_data_out));
  single_register x31 (.data_in(write_data), .write_en(and_31_out), .clock(clock), .data_out(x31_data_out));
  Multiplexer #(.enable("true"), .select(5), .width(32)) multiplexer_1 (
    .in0(x0_data_out), .in1(x1_data_out), .in2(x2_data_out), .in3(x3_data_out), .in4(x4_data_out),
    .in5(x5_data_out), .in6(x6_data_out), .in7(x7_data_out), .in8(x8_data_out), .in9(x9_data_out),
    .in10(x10_data_out), .in11(x11_data_out), .in12(x12_data_out), .in13(x13_data_out), .in14(x14_data_out),
    .in15(x15_data_out), .in16(x16_data_out), .in17(x17_data_out), .in18(x18_data_out), .in19(x19_data_out),
    .in20(x20_data_out), .in21(x21_data_out), .in22(x22_data_out), .in23(x23_data_out), .in24(x24_data_out),
    .in25(x25_data_out), .in26(x26_data_out), .in27(x27_data_out), .in28(x28_data_out), .in29(x29_data_out),
    .in30(x30_data_out), .in31(x31_data_out), .out(read_data_1), .sel(rs1));  // open: en
  Multiplexer #(.enable("true"), .select(5), .width(32)) multiplexer_2 (
    .in0(x0_data_out), .in1(x1_data_out), .in2(x2_data_out), .in3(x3_data_out), .in4(x4_data_out),
    .in5(x5_data_out), .in6(x6_data_out), .in7(x7_data_out), .in8(x8_data_out), .in9(x9_data_out),
    .in10(x10_data_out), .in11(x11_data_out), .in12(x12_data_out), .in13(x13_data_out), .in14(x14_data_out),
    .in15(x15_data_out), .in16(x16_data_out), .in17(x17_data_out), .in18(x18_data_out), .in19(x19_data_out),
    .in20(x20_data_out), .in21(x21_data_out), .in22(x22_data_out), .in23(x23_data_out), .in24(x24_data_out),
    .in25(x25_data_out), .in26(x26_data_out), .in27(x27_data_out), .in28(x28_data_out), .in29(x29_data_out),
    .in30(x30_data_out), .in31(x31_data_out), .out(read_data_2), .sel(rs2));  // open: en
endmodule

module single_register (
  input  [31:0] data_in,
  input  write_en,
  input  clock,
  output [31:0] data_out
);

  Register #(.width(32)) register_1 (.D(data_in), .en(write_en), .clk(clock), .Q(data_out), .clr(1'b0));
endmodule
