// Logisim project Part_1.circ as structural Verilog: 2 circuits, main circuit main
module main (
  input  Cin,
  input  A0,
  input  B0,
  input  A1,
  input  B1,
  input  A2,
  input  B2,
  input  A3,
  input  B3,
  output S0,
  output S1,
  output S2,
  output S3,
  output Cout
);

  wire and_1_out, and_2_out, and_3_out, and_4_out, and_5_out, and_6_out, and_7_out, and_8_out, and_9_out,
       and_10_out, and_11_out, and_12_out, or_1_out, or_2_out, or_3_out, xor_1_out, xor_2_out, xor_3_out,
       xor_4_out;

  xor xor_1 (xor_1_out, Cin, A0);
  xor xor_2 (xor_2_out, or_1_out, A1);
  xor xor_3 (xor_3_out, or_2_out, A2);
  xor xor_4 (xor_4_out, or_3_out, A3);
  and and_1 (and_1_out, A0, B0);
  and and_2 (and_2_out, Cin, A0);
  and and_3 (and_3_out, Cin, B0);
  and and_4 (and_4_out, A1, B1);
  and and_5 (and_5_out, or_1_out, A1);
  and and_6 (and_6_out, or_1_out, B1);
  and and_7 (and_7_out, A2, B2);
  and and_8 (and_8_out, or_2_out, A2);
  and and_9 (and_9_out, or_2_out, B2);
  and and_10 (and_10_out, A3, B3);
  and and_11 (and_11_out, or_3_out, A3);
  and and_12 (and_12_out, or_3_out, B3);
  xor xor_5 (S0, xor_1_out, B0);
  or or_1 (or_1_out, and_1_out, and_2_out, and_3_out);
  xor xor_6 (S1, xor_2_out, B1);
  or or_2 (or_2_out, and_4_out, and_5_out, and_6_out);
  xor xor_7 (S2, xor_3_out, B2);
  or or_3 (or_3_out, and_7_out, and_8_out, and_9_out);
  xor xor_8 (S3, xor_4_out, B3);
  or or_4 (Cout, and_10_out, and_11_out, and_12_out);
endmodule

module main2 (
  input  Cin,
  input  A0,
  input  B0,
  input  A1,
  input  B1,
  input  A2,
  input  B2,
  input  A3,
  input  B3,
  output S0,
  output S1,
  output S2,
  output S3,
  output Cout
);

  wire and_1_out, and_2_out, and_3_out, and_4_out, and_5_out, and_6_out, and_7_out, and_8_out, and_9_out,
       and_10_out, and_11_out, and_12_out, and_13_out, and_14_out, and_15_out, and_16_out, and_17_out,
       and_18_out, and_19_out, and_20_out, and_21_out, and_22_out, and_23_out, and_24_out, and_25_out,
       and_26_out, and_27_out, and_28_out, and_29_out, and_30_out, and_31_out, and_32_out, and_33_out,
       and_34_out, and_35_out, and_36_out, and_37_out, and_38_out, and_39_out, and_40_out, and_41_out,
       and_42_out, and_43_out, and_44_out, and_45_out, and_46_out, and_47_out, and_48_out, and_49_out,
       and_50_out, and_51_out, and_52_out, and_53_out, and_54_out, and_55_out, and_56_out, and_57_out,
       and_58_out, and_59_out, and_60_out, and_61_out, and_62_out, and_63_out, and_64_out, and_65_out,
       and_66_out, and_67_out, and_68_out, and_69_out, and_70_out, and_71_out, and_72_out, and_73_out,
       and_74_out, and_75_out, and_76_out, and_77_out, and_78_out, or_1_out, or_2_out, or_3_out, or_4_out,
       or_5_out, or_6_out, or_7_out, or_8_out, or_9_out, or_10_out, or_11_out, or_12_out, or_13_out,
       or_14_out, or_15_out, or_16_out, or_17_out, or_18_out, or_19_out, or_20_out, or_21_out, or_22_out,
       or_23_out, or_24_out, or_25_out;

  xor odd_parity_1 (S0, Cin, A0, B0);
  and and_1 (and_1_out, A0, B0);
  and and_2 (and_2_out, Cin, A0);
  and and_3 (and_3_out, Cin, B0);
  and and_4 (and_4_out, A0, B0);
  and and_5 (and_5_out, Cin, A0);
  and and_6 (and_6_out, Cin, B0);
  and and_7 (and_7_out, A0, B0);
  and and_8 (and_8_out, Cin, A0);
  and and_9 (and_9_out, Cin, B0);
  and and_10 (and_10_out, A0, B0);
  and and_11 (and_11_out, Cin, A0);
  and and_12 (and_12_out, Cin, B0);
  and and_13 (and_13_out, A0, B0);
  and and_14 (and_14_out, Cin, A0);
  and and_15 (and_15_out, Cin, B0);
  and and_16 (and_16_out, A0, B0);
  and and_17 (and_17_out, Cin, A0);
  and and_18 (and_18_out, Cin, B0);
  and and_19 (and_19_out, A0, B0);
  and and_20 (and_20_out, Cin, A0);
  and and_21 (and_21_out, Cin, B0);
  and and_22 (and_22_out, A0, B0);
  and and_23 (and_23_out, Cin, A0);
  and and_24 (and_24_out, Cin, B0);
  and and_25 (and_25_out, A0, B0);
  and and_26 (and_26_out, Cin, A0);
  and and_27 (and_27_out, Cin, B0);
  and and_28 (and_28_out, A0, B0);
  and and_29 (and_29_out, Cin, A0);
  and and_30 (and_30_out, Cin, B0);
  and and_31 (and_31_out, A0, B0);
  and and_32 (and_32_out, Cin, A0);
  and and_33 (and_33_out, Cin, B0);
  and and_34 (and_34_out, A0, B0);
  and and_35 (and_35_out, Cin, A0);
  and and_36 (and_36_out, Cin, B0);
  and and_37 (and_37_out, A0, B0);
  and and_38 (and_38_out, Cin, A0);
  and and_39 (and_39_out, Cin, B0);
  and and_40 (and_40_out, A0, B0);
  and and_41 (and_41_out, Cin, A0);
  and and_42 (and_42_out, Cin, B0);
  and and_43 (and_43_out, A0, B0);
  and and_44 (and_44_out, Cin, A0);
  and and_45 (and_45_out, Cin, B0);
  or or_1 (or_1_out, and_1_out, and_2_out, and_3_out);
  or or_2 (or_2_out, and_4_out, and_5_out, and_6_out);
  or or_3 (or_3_out, and_7_out, and_8_out, and_9_out);
  or or_4 (or_4_out, and_10_out, and_11_out, and_12_out);
  or or_5 (or_5_out, and_13_out, and_14_out, and_15_out);
  or or_6 (or_6_out, and_16_out, and_17_out, and_18_out);
  or or_7 (or_7_out, and_19_out, and_20_out, and_21_out);
  or or_8 (or_8_out, and_22_out, and_23_out, and_24_out);
  or or_9 (or_9_out, and_25_out, and_26_out, and_27_out);
  or or_10 (or_10_out, and_28_out, and_29_out, and_30_out);
  or or_11 (or_11_out, and_31_out, and_32_out, and_33_out);
  or or_12 (or_12_out, and_34_out, and_35_out, and_36_out);
  or or_13 (or_13_out, and_37_out, and_38_out, and_39_out);
  or or_14 (or_14_out, and_40_out, and_41_out, and_42_out);
  or or_15 (or_15_out, and_43_out, and_44_out, and_45_out);
  xor odd_parity_2 (S1, or_1_out, A1, B1);
  and and_46 (and_46_out, A1, B1);
  and and_47 (and_47_out, or_2_out, A1);
  and and_48 (and_48_out, or_3_out, B1);
  and and_49 (and_49_out, A1, B1);
  and and_50 (and_50_out, or_4_out, A1);
  and and_51 (and_51_out, or_5_out, B1);
  and and_52 (and_52_out, A1, B1);
  and and_53 (and_53_out, or_6_out, A1);
  and and_54 (and_54_out, or_7_out, B1);
  and and_55 (and_55_out, A1, B1);
  and and_56 (and_56_out, or_8_out, A1);
  and and_57 (and_57_out, or_9_out, B1);
  and and_58 (and_58_out, A1, B1);
  and and_59 (and_59_out, or_10_out, A1);
  and and_60 (and_60_out, or_11_out, B1);
  and and_61 (and_61_out, A1, B1);
  and and_62 (and_62_out, or_12_out, A1);
  and and_63 (and_63_out, or_13_out, B1);
  and and_64 (and_64_out, A1, B1);
  and and_65 (and_65_out, or_14_out, A1);
  and and_66 (and_66_out, or_15_out, B1);
  or or_16 (or_16_out, and_46_out, and_47_out, and_48_out);
  xor odd_parity_3 (S2, or_16_out, A2, B2);
  and and_67 (and_67_out, A2, B2);
  or or_17 (or_17_out, and_49_out, and_50_out, and_51_out);
  and and_68 (and_68_out, or_17_out, A2);
  or or_18 (or_18_out, and_52_out, and_53_out, and_54_out);
  and and_69 (and_69_out, or_18_out, B2);
  and and_70 (and_70_out, A2, B2);
  or or_19 (or_19_out, and_55_out, and_56_out, and_57_out);
  and and_71 (and_71_out, or_19_out, A2);
  or or_20 (or_20_out, and_58_out, and_59_out, and_60_out);
  and and_72 (and_72_out, or_20_out, B2);
  and and_73 (and_73_out, A2, B2);
  or or_21 (or_21_out, and_61_out, and_62_out, and_63_out);
  and and_74 (and_74_out, or_21_out, A2);
  or or_22 (or_22_out, and_64_out, and_65_out, and_66_out);
  and and_75 (and_75_out, or_22_out, B2);
  or or_23 (or_23_out, and_67_out, and_68_out, and_69_out);
  or or_24 (or_24_out, and_70_out, and_71_out, and_72_out);
  or or_25 (or_25_out, and_73_out, and_74_out, and_75_out);
  xor odd_parity_4 (S3, or_23_out, A3, B3);
  and and_76 (and_76_out, A3, B3);
  and and_77 (and_77_out, or_24_out, A3);
  and and_78 (and_78_out, or_25_out, B3);
  or or_26 (Cout, and_76_out, and_77_out, and_78_out);
endmodule
