// Logisim project processor.circ as structural Verilog: 11 circuits, main circuit main
module main (
  input  PC_reset,
  input  Reg_file_reset,
  output [4:0] rs1,
  output [4:0] rs2,
  output [4:0] rd,
  output [31:0] immediate_value,
  output [31:0] alu_output,
  output [31:0] Instruction,
  output [31:0] data_in_rs1,
  output [31:0] write_data,
  output [31:0] data_in_rs2
);

  wire alu_1_zero, and_1_out, Clk_out, control_unit_1_alusrc, control_unit_1_branch, control_unit_1_memread,
       control_unit_1_memtoreg, control_unit_1_memwrite, control_unit_1_regwrite;
  wire [1:0] control_unit_1_aluop;
  wire [3:0] control_unit_1_alu_control;
  wire [15:0] register_1_q;
  wire [31:0] adder_1_out, adder_2_out, bit_extender_1_out, memory_unit_1_read_data, multiplexer_1_out,
       multiplexer_2_out, shifter_1_out;

  Clock Clk (.out(Clk_out));
  Register #(.width(16)) register_1 (
    .D(multiplexer_2_out[15:0]), .en(1'b1), .clk(Clk_out), .Q(register_1_q), .clr(PC_reset));
  Instr_memory instr_memory_1 (.Program_Counter(register_1_q), .Instruction(Instruction));
  assign bit_extender_1_out = {{16{1'b0}}, register_1_q};  // Bit_Extender bit_extender_1
  register_file register_file_1 (
    .rs1(Instruction[19:15]), .rs2(Instruction[24:20]), .rd(Instruction[11:7]),
    .RegWEn(control_unit_1_regwrite), .clock(Clk_out), .Reg_file_reset(Reg_file_reset),
    .write_data(write_data), .read_data_1(data_in_rs1), .read_data_2(data_in_rs2));
  immgen immgen_1 (.ALUOp(control_unit_1_aluop), .Instruction(Instruction), .Immediate_Val(immediate_value));
  control_unit control_unit_1 (
    .Instruction(Instruction), .ALUSrc(control_unit_1_alusrc), .MemtoReg(control_unit_1_memtoreg),
    .RegWrite(control_unit_1_regwrite), .MemRead(control_unit_1_memread), .MemWrite(control_unit_1_memwrite),
    .Branch(control_unit_1_branch), .ALUOp(control_unit_1_aluop), .ALU_control(control_unit_1_alu_control));  // open: RegDst
  Shifter #(.shift("lr"), .width(32)) shifter_1 (.in(immediate_value), .\dist (5'b00010), .out(shifter_1_out));
  Multiplexer #(.width(32)) multiplexer_1 (
    .in0(data_in_rs2), .in1(immediate_value), .out(multiplexer_1_out), .sel(control_unit_1_alusrc));
  Adder #(.width(32)) adder_1 (.a(32'h1), .b(bit_extender_1_out), .out(adder_1_out));  // open: cin, cout
  Adder #(.width(32)) adder_2 (.a(bit_extender_1_out), .b(shifter_1_out), .out(adder_2_out));  // open: cin, cout
  alu alu_1 (
    .A(data_in_rs1), .ALU_control(control_unit_1_alu_control), .B(multiplexer_1_out), .Result(alu_output),
    .Zero(alu_1_zero));  // open: over
  and and_1 (and_1_out, control_unit_1_branch, alu_1_zero);
  Multiplexer #(.width(32)) multiplexer_2 (
    .in0(adder_1_out), .in1(adder_2_out), .out(multiplexer_2_out), .sel(and_1_out));
  memory_unit memory_unit_1 (
    .address(alu_output[15:0]), .mem_read(control_unit_1_memread), .mem_write(control_unit_1_memwrite),
    .clock(Clk_out), .write_data(data_in_rs2), .read_data(memory_unit_1_read_data));
  Multiplexer #(.width(32)) multiplexer_3 (
    .in0(alu_output), .in1(memory_unit_1_read_data), .out(write_data), .sel(control_unit_1_memtoreg));

  assign rd = Instruction[11:7];
  assign rs1 = Instruction[19:15];
  assign rs2 = Instruction[24:20];

  // Notes on the sheet:
  //   Nikhil Zawar - 2022CS11106
  //   Yash bansal :- 2022CS51133
endmodule

module alucontrol (
  input  [1:0] ALUOp,
  input  [2:0] func3,
  input  [6:0] func7,
  output [3:0] ALU_Control
);

  Multiplexer #(.select(2), .width(4)) multiplexer_1 (
    .in0(4'b0000), .in1(4'b1000), .in2({func7[5], func3}), .in3({1'b0, func3}), .out(ALU_Control), .sel(ALUOp));

  // Notes on the sheet:
  //   R- 10
  //   lw/sw - 00
  //   imm- 11
  //   beq - 01
  //   subtract ka alu_control is 1000
endmodule

module control_signals (
  input  [6:0] Opcode,
  output RegDst,
  output ALUSrc,
  output MemtoReg,
  output RegWrite,
  output MemRead,
  output MemWrite,
  output Branch,
  output [1:0] ALUOp
);

  wire Imm_11_out, not_1_out, not_2_out, not_3_out, not_4_out, not_5_out, not_6_out, not_7_out, not_8_out,
       not_9_out, not_10_out, not_11_out, not_12_out, not_13_out, not_14_out, not_15_out, not_16_out,
       not_17_out, not_18_out, not_19_out, Rtype_10_out;

  not not_1 (not_1_out, Opcode[2]);
  not not_2 (not_2_out, Opcode[3]);
  and Rtype_10 (Rtype_10_out, Opcode[1], not_1_out, not_2_out, Opcode[4], Opcode[5], not_3_out);
  not not_3 (not_3_out, Opcode[6]);
  not not_4 (not_4_out, Opcode[2]);
  not not_5 (not_5_out, Opcode[3]);
  and lw_00 (MemRead, Opcode[1], not_4_out, not_5_out, not_6_out, not_7_out, not_8_out);
  not not_6 (not_6_out, Opcode[4]);
  not not_7 (not_7_out, Opcode[5]);
  not not_8 (not_8_out, Opcode[6]);
  not not_9 (not_9_out, Opcode[2]);
  not not_10 (not_10_out, Opcode[3]);
  and sw_00 (MemWrite, Opcode[1], not_9_out, not_10_out, not_12_out, Opcode[5], not_11_out);
  not not_11 (not_11_out, Opcode[6]);
  not not_12 (not_12_out, Opcode[4]);
  not not_13 (not_13_out, Opcode[2]);
  not not_14 (not_14_out, Opcode[3]);
  and Imm_11 (Imm_11_out, Opcode[1], not_13_out, not_14_out, Opcode[4], not_15_out, not_16_out);
  not not_15 (not_15_out, Opcode[5]);
  not not_16 (not_16_out, Opcode[6]);
  not not_17 (not_17_out, Opcode[2]);
  not not_18 (not_18_out, Opcode[3]);
  not not_19 (not_19_out, Opcode[4]);
  and beq_01 (Branch, Opcode[1], not_17_out, not_18_out, not_19_out, Opcode[5], Opcode[6]);
  or or_1 (ALUSrc, MemRead, MemWrite, Imm_11_out);
  or or_2 (RegWrite, Rtype_10_out, MemRead, Imm_11_out);
  or or_3 (ALUOp[0], Branch, Imm_11_out);
  or or_4 (ALUOp[1], Imm_11_out, Rtype_10_out);

  assign MemtoReg = MemRead;
endmodule

module control_unit (
  input  [31:0] Instruction,
  output RegDst,
  output ALUSrc,
  output MemtoReg,
  output RegWrite,
  output MemRead,
  output MemWrite,
  output Branch,
  output [1:0] ALUOp,
  output [3:0] ALU_control
);

  control_signals control_signals_1 (
    .Opcode(Instruction[6:0]), .RegDst(RegDst), .ALUSrc(ALUSrc), .MemtoReg(MemtoReg), .RegWrite(RegWrite),
    .MemRead(MemRead), .MemWrite(MemWrite), .Branch(Branch), .ALUOp(ALUOp));
  alucontrol alucontrol_1 (
    .ALUOp(ALUOp), .func3(Instruction[14:12]), .func7(Instruction[31:25]), .ALU_Control(ALU_control));
endmodule

module Instr_memory (
  input  [15:0] Program_Counter,
  output [31:0] Instruction
);

  ROM #(.addrWidth(16), .dataWidth(32)) rom_1 (.addr(Program_Counter), .data(Instruction));

  // Notes on the sheet:
  //   contents of rom_1 (hex, n*v repeats v):
  //   208093 508093 108133 618193 11a523 a1a203 728293 520663 738393
endmodule

module alu (
  input  [31:0] A,
  input  [3:0] ALU_control,
  input  [31:0] B,
  output [31:0] Result,
  output Zero,
  output over
);

  wire comparator_1_lt, comparator_2_lt;
  wire [31:0] adder_1_out, and_1_out, bit_extender_1_out, bit_extender_2_out, or_1_out, shifter_1_out,
       shifter_2_out, shifter_3_out, subtractor_1_out, xor_1_out;

  Adder #(.width(32)) adder_1 (.a(A), .b(B), .out(adder_1_out));  // open: cin, cout
  Shifter #(.width(32)) shifter_1 (.in(A), .\dist (B[4:0]), .out(shifter_1_out));
  Comparator #(.width(32)) comparator_1 (.a(A), .b(B), .lt(comparator_1_lt));  // open: gt, eq
  Comparator #(.mode("unsigned"), .width(32)) comparator_2 (.a(A), .b(B), .lt(comparator_2_lt));  // open: gt, eq
  assign xor_1_out = A ^ B;  // XOR_Gate xor_1, 32 bits wide
  Shifter #(.shift("lr"), .width(32)) shifter_2 (.in(A), .\dist (B[4:0]), .out(shifter_2_out));
  assign or_1_out = A | B;  // OR_Gate or_1, 32 bits wide
  assign and_1_out = A & B;  // AND_Gate and_1, 32 bits wide
  Subtractor #(.width(32)) subtractor_1 (.a(A), .b(B), .out(subtractor_1_out));  // open: bin, bout
  Shifter #(.shift("ar"), .width(32)) shifter_3 (.in(A), .\dist (B[4:0]), .out(shifter_3_out));
  assign bit_extender_1_out = {{31{comparator_1_lt}}, comparator_1_lt};  // Bit_Extender bit_extender_1
  assign bit_extender_2_out = {{31{comparator_2_lt}}, comparator_2_lt};  // Bit_Extender bit_extender_2
  Multiplexer #(.select(4), .width(32)) multiplexer_1 (
    .in0(adder_1_out), .in1(shifter_1_out), .in2(bit_extender_1_out), .in3(bit_extender_2_out),
    .in4(xor_1_out), .in5(shifter_2_out), .in6(or_1_out), .in7(and_1_out), .in8(subtractor_1_out),
    .in13(shifter_3_out), .out(Result), .sel(ALU_control));  // open: in9, in10, in11, in12, in14, in15
  Comparator #(.width(32)) comparator_3 (.a(Result), .b({32{1'b0}}), .eq(Zero));  // open: gt, lt
  overflow overflow_1 (.in_1(ALU_control), .ans(adder_1_out), .A(A), .B(B), .over(over));

  // Notes on the sheet:
  //   0 -add
  //   1- sll
  //   2 - slt signed
  //   4 - xor
  //   6 - or
  //   7 - and
  //   8 - sub
  //   13 - sra
  //   3 - slt unsigned
  //   5 - srl - unsigned shift
  //   0 -add
  //   1- sll
  //   2 - slt signed
  //   3 - slt unsigned
  //   4 - xor
  //   6 - or
  //   7 - and
  //   8 - sub
  //   13 - sra
  //   5 - srl - unsigned shift
endmodule

module overflow (
  input  [3:0] in_1,
  input  [31:0] ans,
  input  [31:0] A,
  input  [31:0] B,
  output over
);

  wire and_1_out, and_2_out, not_1_out, not_2_out, not_3_out, not_4_out, not_5_out, xor_1_out, xor_2_out;

  xor xor_1 (xor_1_out, A[31], B[31]);
  not not_1 (not_1_out, xor_1_out);
  xor xor_2 (xor_2_out, ans[31], B[31]);
  not not_2 (not_2_out, in_1[3]);
  not not_3 (not_3_out, in_1[2]);
  not not_4 (not_4_out, in_1[1]);
  not not_5 (not_5_out, in_1[0]);
  and and_1 (and_1_out, not_1_out, xor_2_out);
  and and_2 (and_2_out, not_1_out, and_1_out);
  and and_3 (over, not_2_out, not_3_out, not_4_out, not_5_out, and_2_out);
endmodule

module single_register (
  input  [31:0] data_in,
  input  write_en,
  input  clock,
  input  reset,
  output [31:0] data_out
);

  Register #(.width(32)) register_1 (.D(data_in), .en(write_en), .clk(clock), .Q(data_out), .clr(reset));
endmodule

module register_file (
  input  [4:0] rs1,
  input  [4:0] rs2,
  input  [4:0] rd,
  input  RegWEn,
  input  clock,
  input  Reg_file_reset,
  input  [31:0] write_data,
  output [31:0] read_data_1,
  output [31:0] read_data_2
);

  wire and_1_out, and_2_out, and_3_out, and_4_out, and_5_out, and_6_out, and_7_out, and_8_out, and_9_out,
       and_10_out, and_11_out, and_12_out, and_13_out, and_14_out, and_15_out, and_16_out, and_17_out,
       and_18_out, and_19_out, and_20_out, and_21_out, and_22_out, and_23_out, and_24_out, and_25_out,
       and_26_out, and_27_out, and_28_out, and_29_out, and_30_out, and_31_out;
  wire [31:0] shifter_1_out, x0_data_out, x1_data_out, x2_data_out, x3_data_out, x4_data_out, x5_data_out,
       x6_data_out, x7_data_out, x8_data_out, x9_data_out, x10_data_out, x11_data_out, x12_data_out,
       x13_data_out, x14_data_out, x15_data_out, x16_data_out, x17_data_out, x18_data_out, x19_data_out,
       x20_data_out, x21_data_out, x22_data_out, x23_data_out, x24_data_out, x25_data_out, x26_data_out,
       x27_data_out, x28_data_out, x29_data_out, x30_data_out, x31_data_out;

  Shifter #(.width(32)) shifter_1 (.in(32'h1), .\dist (rd), .out(shifter_1_out));
  and and_1 (and_1_out, RegWEn, shifter_1_out[1]);
  and and_2 (and_2_out, RegWEn, shifter_1_out[2]);
  and and_3 (and_3_out, RegWEn, shifter_1_out[3]);
  and and_4 (and_4_out, RegWEn, shifter_1_out[4]);
  and and_5 (and_5_out, RegWEn, shifter_1_out[5]);
  and and_6 (and_6_out, RegWEn, shifter_1_out[6]);
  and and_7 (and_7_out, RegWEn, shifter_1_out[7]);
  and and_8 (and_8_out, RegWEn, shifter_1_out[8]);
  and and_9 (and_9_out, RegWEn, shifter_1_out[9]);
  and and_10 (and_10_out, RegWEn, shifter_1_out[10]);
  and and_11 (and_11_out, RegWEn, shifter_1_out[11]);
  and and_12 (and_12_out, RegWEn, shifter_1_out[12]);
  and and_13 (and_13_out, RegWEn, shifter_1_out[13]);
  and and_14 (and_14_out, RegWEn, shifter_1_out[14]);
  and and_15 (and_15_out, RegWEn, shifter_1_out[15]);
  and and_16 (and_16_out, RegWEn, shifter_1_out[16]);
  and and_17 (and_17_out, RegWEn, shifter_1_out[17]);
  and and_18 (and_18_out, RegWEn, shifter_1_out[18]);
  and and_19 (and_19_out, RegWEn, shifter_1_out[19]);
  and and_20 (and_20_out, RegWEn, shifter_1_out[20]);
  and and_21 (and_21_out, RegWEn, shifter_1_out[21]);
  and and_22 (and_22_out, RegWEn, shifter_1_out[22]);
  and and_23 (and_23_out, RegWEn, shifter_1_out[23]);
  and and_24 (and_24_out, RegWEn, shifter_1_out[24]);
  and and_25 (and_25_out, RegWEn, shifter_1_out[25]);
  and and_26 (and_26_out, RegWEn, shifter_1_out[26]);
  and and_27 (and_27_out, RegWEn, shifter_1_out[27]);
  and and_28 (and_28_out, RegWEn, shifter_1_out[28]);
  and and_29 (and_29_out, RegWEn, shifter_1_out[29]);
  and and_30 (and_30_out, RegWEn, shifter_1_out[30]);
  and and_31 (and_31_out, RegWEn, shifter_1_out[31]);
  single_register x0 (
    .data_in({32{1'b0}}), .write_en(1'b1), .clock(clock), .reset(Reg_file_reset), .data_out(x0_data_out));
  single_register x1 (
    .data_in(write_data), .write_en(and_1_out), .clock(clock), .reset(Reg_file_reset), .data_out(x1_data_out));
  single_register x2 (
    .data_in(write_data), .write_en(and_2_out), .clock(clock), .reset(Reg_file_reset), .data_out(x2_data_out));
  single_register x3 (
    .data_in(write_data), .write_en(and_3_out), .clock(clock), .reset(Reg_file_reset), .data_out(x3_data_out));
  single_register x4 (
    .data_in(write_data), .write_en(and_4_out), .clock(clock), .reset(Reg_file_reset), .data_out(x4_data_out));
  single_register x5 (
    .data_in(write_data), .write_en(and_5_out), .clock(clock), .reset(Reg_file_reset), .data_out(x5_data_out));
  single_register x6 (
    .data_in(write_data), .write_en(and_6_out), .clock(clock), .reset(Reg_file_reset), .data_out(x6_data_out));
  single_register x7 (
    .data_in(write_data), .write_en(and_7_out), .clock(clock), .reset(Reg_file_reset), .data_out(x7_data_out));
  single_register x8 (
    .data_in(write_data), .write_en(and_8_out), .clock(clock), .reset(Reg_file_reset), .data_out(x8_data_out));
  single_register x9 (
    .data_in(write_data), .write_en(and_9_out), .clock(clock), .reset(Reg_file_reset), .data_out(x9_data_out));
  single_register x10 (
    .data_in(write_data), .write_en(and_10_out), .clock(clock), .reset(Reg_file_reset),
    .data_out(x10_data_out));
  single_register x11 (
    .data_in(write_data), .write_en(and_11_out), .clock(clock), .reset(Reg_file_reset),
    .data_out(x11_data_out));
  single_register x12 (
    .data_in(write_data), .write_en(and_12_out), .clock(clock), .reset(Reg_file_reset),
    .data_out(x12_data_out));
  single_register x13 (
    .data_in(write_data), .write_en(and_13_out), .clock(clock), .reset(Reg_file_reset),
    .data_out(x13_data_out));
  single_register x14 (
    .data_in(write_data), .write_en(and_14_out), .clock(clock), .reset(Reg_file_reset),
    .data_out(x14_data_out));
  single_register x15 (
    .data_in(write_data), .write_en(and_15_out), .clock(clock), .reset(Reg_file_reset),
    .data_out(x15_data_out));
  single_register x16 (
    .data_in(write_data), .write_en(and_16_out), .clock(clock), .reset(Reg_file_reset),
    .data_out(x16_data_out));
  single_register x17 (
    .data_in(write_data), .write_en(and_17_out), .clock(clock), .reset(Reg_file_reset),
    .data_out(x17_data_out));
  single_register x18 (
    .data_in(write_data), .write_en(and_18_out), .clock(clock), .reset(Reg_file_reset),
    .data_out(x18_data_out));
  single_register x19 (
    .data_in(write_data), .write_en(and_19_out), .clock(clock), .reset(Reg_file_reset),
    .data_out(x19_data_out));
  single_register x20 (
    .data_in(write_data), .write_en(and_20_out), .clock(clock), .reset(Reg_file_reset),
    .data_out(x20_data_out));
  single_register x21 (
    .data_in(write_data), .write_en(and_21_out), .clock(clock), .reset(Reg_file_reset),
    .data_out(x21_data_out));
  single_register x22 (
    .data_in(write_data), .write_en(and_22_out), .clock(clock), .reset(Reg_file_reset),
    .data_out(x22_data_out));
  single_register x23 (
    .data_in(write_data), .write_en(and_23_out), .clock(clock), .reset(Reg_file_reset),
    .data_out(x23_data_out));
  single_register x24 (
    .data_in(write_data), .write_en(and_24_out), .clock(clock), .reset(Reg_file_reset),
    .data_out(x24_data_out));
  single_register x25 (
    .data_in(write_data), .write_en(and_25_out), .clock(clock), .reset(Reg_file_reset),
    .data_out(x25_data_out));
  single_register x26 (
    .data_in(write_data), .write_en(and_26_out), .clock(clock), .reset(Reg_file_reset),
    .data_out(x26_data_out));
  single_register x27 (
    .data_in(write_data), .write_en(and_27_out), .clock(clock), .reset(Reg_file_reset),
    .data_out(x27_data_out));
  single_register x28 (
    .data_in(write_data), .write_en(and_28_out), .clock(clock), .reset(Reg_file_reset),
    .data_out(x28_data_out));
  single_register x29 (
    .data_in(write_data), .write_en(and_29_out), .clock(clock), .reset(Reg_file_reset),
    .data_out(x29_data_out));
  single_register x30 (
    .data_in(write_data), .write_en(and_30_out), .clock(clock), .reset(Reg_file_reset),
    .data_out(x30_data_out));
  single_register x31 (
    .data_in(write_data), .write_en(and_31_out), .clock(clock), .reset(Reg_file_reset),
    .data_out(x31_data_out));
  Multiplexer #(.enable("true"), .select(5), .width(32)) multiplexer_1 (
    .in0(x0_data_out), .in1(x1_data_out), .in2(x2_data_out), .in3(x3_data_out), .in4(x4_data_out),
    .in5(x5_data_out), .in6(x6_data_out), .in7(x7_data_out), .in8(x8_data_out), .in9(x9_data_out),
    .in10(x10_data_out), .in11(x11_data_out), .in12(x12_data_out), .in13(x13_data_out), .in14(x14_data_out),
    .in15(x15_data_out), .in16(x16_data_out), .in17(x17_data_out), .in18(x18_data_out), .in19(x19_data_out),
    .in20(x20_data_out), .in21(x21_data_out), .in22(x22_data_out), .in23(x23_data_out), .in24(x24_data_out),
    .in25(x25_data_out), .in26(x26_data_out), .in27(x27_data_out), .in28(x28_data_out), .in29(x29_data_out),
    .in30(x30_data_out), .in31(x31_data_out), .out(read_data_1), .sel(rs1));  // open: en
  Multiplexer #(.enable("true"), .select(5), .width(32)) multiplexer_2 (
    .in0(x0_data_out), .in1(x1_data_out), .in2(x2_data_out), .in3(x3_data_out), .in4(x4_data_out),
    .in5(x5_data_out), .in6(x6_data_out), .in7(x7_data_out), .in8(x8_data_out), .in9(x9_data_out),
    .in10(x10_data_out), .in11(x11_data_out), .in12(x12_data_out), .in13(x13_data_out), .in14(x14_data_out),
    .in15(x15_data_out), .in16(x16_data_out), .in17(x17_data_out), .in18(x18_data_out), .in19(x19_data_out),
    .in20(x20_data_out), .in21(x21_data_out), .in22(x22_data_out), .in23(x23_data_out), .in24(x24_data_out),
    .in25(x25_data_out), .in26(x26_data_out), .in27(x27_data_out), .in28(x28_data_out), .in29(x29_data_out),
    .in30(x30_data_out), .in31(x31_data_out), .out(read_data_2), .sel(rs2));  // open: en
endmodule

module immgen (
  input  [1:0] ALUOp,
  input  [31:0] Instruction,
  output [31:0] Immediate_Val
);

  wire [7:7] undriven;
  wire [11:0] multiplexer_1_out;
  wire [31:0] bit_extender_1_out, bit_extender_2_out, bit_extender_3_out;

  Multiplexer #(.width(12)) multiplexer_1 (
    .in0({Instruction[31:28], Instruction[31], Instruction[26:20]}),
    .in1({Instruction[31:28], undriven[7], Instruction[26:25], Instruction[11:7]}), .out(multiplexer_1_out),
    .sel(Instruction[5]));
  assign bit_extender_1_out = {{20{Instruction[31]}}, {Instruction[31:28], Instruction[31], Instruction[26:20]}};  // Bit_Extender bit_extender_1
  assign bit_extender_2_out = {{20{multiplexer_1_out[11]}}, multiplexer_1_out};  // Bit_Extender bit_extender_2
  assign bit_extender_3_out = {{19{Instruction[31]}}, {Instruction[31], Instruction[7], Instruction[30:28], Instruction[31], Instruction[26:25], Instruction[11:8], 1'b0}};  // Bit_Extender bit_extender_3
  Multiplexer #(.select(2), .width(32)) multiplexer_2 (
    .in0(bit_extender_2_out), .in1(bit_extender_3_out), .in3(bit_extender_1_out), .out(Immediate_Val),
    .sel(ALUOp));  // open: in2

  assign Instruction[27] = Instruction[31];

  // Notes on the sheet:
  //   S type
  //   I type
endmodule

module memory_unit (
  input  [15:0] address,
  input  mem_read,
  input  mem_write,
  input  clock,
  input  [31:0] write_data,
  output [31:0] read_data
);

  RAM #(.addrWidth(16), .asyncread("true"), .dataWidth(32)) ram_1 (
    .addr(address), .we(mem_write), .oe(mem_read), .clk(clock), .din(write_data), .dout(read_data));
endmodule
